// Logisim project 1.circ as structural Verilog: 1 circuit, main circuit main
module main (
  input  A,
  input  B,
  input  C
);

  wire transistor_1_out, transistor_3_out, transistor_5_out, transistor_7_out, transistor_8_out,
       transistor_9_out, transistor_10_out, transistor_11_out, transistor_14_out, transistor_15_out,
       transistor_16_out, transistor_17_out, transistor_18_out, transistor_28_out, transistor_29_out;

  Transistor transistor_1 (.in(1'b1), .out(transistor_1_out), .gate(A));
  Transistor #(.\type ("n")) transistor_2 (.in(1'b0), .out(transistor_1_out), .gate(A));
  Transistor transistor_3 (.in(1'b1), .out(transistor_3_out), .gate(B));
  Transistor #(.\type ("n")) transistor_4 (.in(1'b0), .out(transistor_3_out), .gate(B));
  Transistor transistor_5 (.in(1'b1), .out(transistor_5_out), .gate(C));
  Transistor #(.\type ("n")) transistor_6 (.in(1'b0), .out(transistor_5_out), .gate(C));
  Transistor transistor_7 (.in(1'b1), .out(transistor_7_out), .gate(A));
  Transistor transistor_8 (.in(transistor_7_out), .out(transistor_8_out), .gate(B));
  Transistor transistor_9 (.in(transistor_8_out), .out(transistor_9_out), .gate(transistor_5_out));
  Transistor transistor_10 (.in(1'b1), .out(transistor_10_out), .gate(A));
  Transistor transistor_11 (.in(transistor_10_out), .out(transistor_11_out), .gate(transistor_3_out));
  Transistor transistor_12 (.in(transistor_11_out), .out(transistor_9_out), .gate(C));
  Transistor #(.\type ("n")) transistor_13 (.in(transistor_14_out), .out(transistor_9_out), .gate(A));
  Transistor #(.\type ("n")) transistor_14 (.in(transistor_15_out), .out(transistor_14_out), .gate(A));
  Transistor #(.\type ("n")) transistor_15 (.in(transistor_16_out), .out(transistor_15_out), .gate(transistor_1_out));
  Transistor #(.\type ("n")) transistor_16 (.in(1'b0), .out(transistor_16_out), .gate(transistor_1_out));
  Transistor transistor_17 (.in(1'b1), .out(transistor_17_out), .gate(transistor_1_out));
  Transistor transistor_18 (.in(transistor_17_out), .out(transistor_18_out), .gate(B));
  Transistor transistor_19 (.in(transistor_18_out), .out(transistor_9_out), .gate(C));
  Transistor #(.\type ("n")) transistor_20 (.in(transistor_14_out), .out(transistor_9_out), .gate(B));
  Transistor #(.\type ("n")) transistor_21 (.in(transistor_14_out), .out(transistor_9_out), .gate(transistor_5_out));
  Transistor #(.\type ("n")) transistor_22 (.in(transistor_15_out), .out(transistor_14_out), .gate(transistor_3_out));
  Transistor #(.\type ("n")) transistor_23 (.in(transistor_15_out), .out(transistor_14_out), .gate(C));
  Transistor #(.\type ("n")) transistor_24 (.in(transistor_16_out), .out(transistor_15_out), .gate(B));
  Transistor #(.\type ("n")) transistor_25 (.in(transistor_16_out), .out(transistor_15_out), .gate(C));
  Transistor #(.\type ("n")) transistor_26 (.in(1'b0), .out(transistor_16_out), .gate(transistor_3_out));
  Transistor #(.\type ("n")) transistor_27 (.in(1'b0), .out(transistor_16_out), .gate(transistor_5_out));
  Transistor transistor_28 (.in(1'b1), .out(transistor_28_out), .gate(transistor_1_out));
  Transistor transistor_29 (.in(transistor_28_out), .out(transistor_29_out), .gate(transistor_3_out));
  Transistor transistor_30 (.in(transistor_29_out), .out(transistor_9_out), .gate(transistor_5_out));
  // Probe on transistor_9_out
endmodule
