// Logisim project 4.circ as structural Verilog: 1 circuit, main circuit main
module main (
  input  in_1,
  input  in_2,
  input  in_3
);

  wire transistor_1_out, transistor_3_out, transistor_4_out, transistor_8_out, transistor_9_out;

  Transistor transistor_1 (.in(1'b1), .out(transistor_1_out), .gate(in_2));
  Transistor #(.\type ("n")) transistor_2 (.in(1'b0), .out(transistor_1_out), .gate(in_2));
  Transistor transistor_3 (.in(1'b1), .out(transistor_3_out), .gate(in_1));
  Transistor transistor_4 (.in(1'b1), .out(transistor_4_out), .gate(transistor_1_out));
  Transistor transistor_5 (.in(1'b1), .out(transistor_3_out), .gate(in_2));
  Transistor transistor_6 (.in(transistor_4_out), .out(transistor_3_out), .gate(in_3));
  Transistor #(.\type ("n")) transistor_7 (.in(transistor_8_out), .out(transistor_3_out), .gate(in_1));
  Transistor #(.\type ("n")) transistor_8 (.in(transistor_9_out), .out(transistor_8_out), .gate(in_2));
  Transistor #(.\type ("n")) transistor_9 (.in(1'b0), .out(transistor_9_out), .gate(transistor_1_out));
  Transistor #(.\type ("n")) transistor_10 (.in(1'b0), .out(transistor_9_out), .gate(in_3));
  // Probe on transistor_3_out
endmodule
