// Logisim project 2.circ as structural Verilog: 1 circuit, main circuit main
module main (
  input  A,
  input  B,
  input  C
);

  wire transistor_1_out, transistor_3_out, transistor_5_out, transistor_7_out, transistor_8_out,
       transistor_9_out, transistor_12_out, transistor_13_out, transistor_14_out;

  Transistor transistor_1 (.in(1'b1), .out(transistor_1_out), .gate(A));
  Transistor #(.\type ("n")) transistor_2 (.in(1'b0), .out(transistor_1_out), .gate(A));
  Transistor transistor_3 (.in(1'b1), .out(transistor_3_out), .gate(B));
  Transistor #(.\type ("n")) transistor_4 (.in(1'b0), .out(transistor_3_out), .gate(B));
  Transistor transistor_5 (.in(1'b1), .out(transistor_5_out), .gate(C));
  Transistor #(.\type ("n")) transistor_6 (.in(1'b0), .out(transistor_5_out), .gate(C));
  Transistor transistor_7 (.in(1'b1), .out(transistor_7_out), .gate(transistor_1_out));
  Transistor transistor_8 (.in(1'b1), .out(transistor_8_out), .gate(transistor_1_out));
  Transistor transistor_9 (.in(transistor_7_out), .out(transistor_9_out), .gate(transistor_3_out));
  Transistor transistor_10 (.in(transistor_8_out), .out(transistor_9_out), .gate(transistor_5_out));
  Transistor #(.\type ("n")) transistor_11 (.in(transistor_12_out), .out(transistor_9_out), .gate(transistor_1_out));
  Transistor #(.\type ("n")) transistor_12 (.in(transistor_13_out), .out(transistor_12_out), .gate(transistor_1_out));
  Transistor #(.\type ("n")) transistor_13 (.in(1'b0), .out(transistor_13_out), .gate(transistor_3_out));
  Transistor transistor_14 (.in(1'b1), .out(transistor_14_out), .gate(transistor_3_out));
  Transistor transistor_15 (.in(transistor_14_out), .out(transistor_9_out), .gate(transistor_5_out));
  // Probe on transistor_9_out
  Transistor #(.\type ("n")) transistor_16 (.in(transistor_12_out), .out(transistor_9_out), .gate(transistor_3_out));
  Transistor #(.\type ("n")) transistor_17 (.in(transistor_13_out), .out(transistor_12_out), .gate(transistor_5_out));
  Transistor #(.\type ("n")) transistor_18 (.in(1'b0), .out(transistor_13_out), .gate(transistor_5_out));
endmodule
