// Logisim project 3.circ as structural Verilog: 1 circuit, main circuit main
module main (
  input  C
);

  wire transistor_1_out;

  Transistor transistor_1 (.in(1'b1), .out(transistor_1_out), .gate(C));
  // Probe on transistor_1_out
  Transistor #(.\type ("n")) transistor_2 (.in(1'b0), .out(transistor_1_out), .gate(C));
endmodule
